// Logisim project lab1.circ as structural Verilog: 3 circuits, main circuit main
module main (
  input  [4:0] Read_Register_1,
  input  [4:0] Read_Register_2,
  input  [4:0] Write_Register,
  input  [31:0] in_4,
  input  RegWrite,
  input  [31:0] in_6,
  output [31:0] out_7,
  output [31:0] out_8,
  output [31:0] out_9,
  output [31:0] out_10
);

  wire CLK_out;

  register_file register_file_1 (
    .RegWrite(RegWrite), .in_3(in_4), .in_4(in_6), .CLK(CLK_out), .read_register1(Read_Register_1),
    .read_register2(Read_Register_2), .out_8(out_7), .out_9(out_8), .out_10(out_9), .out_11(out_10),
    .Write_Register(Write_Register));
  Clock CLK (.out(CLK_out));

  // Notes on the sheet:
  //   Write Data
  //   Register File
  //   Read Data 1
  //   Read Data 2
endmodule

module register_file (
  input  RegWrite,
  input  [4:0] Write_Register,
  input  [31:0] in_3,
  input  [31:0] in_4,
  input  CLK,
  input  [4:0] read_register1,
  input  [4:0] read_register2,
  output [31:0] out_8,
  output [31:0] out_9,
  output [31:0] out_10,
  output [31:0] out_11
);

  wire decoder_1_out0, decoder_1_out1, decoder_1_out2, decoder_1_out3, decoder_1_out4, decoder_1_out5,
       decoder_1_out6, decoder_1_out7, decoder_1_out8, decoder_1_out9, decoder_1_out10, decoder_1_out11,
       decoder_1_out12, decoder_1_out13, decoder_1_out14, decoder_1_out15, decoder_1_out16, decoder_1_out17,
       decoder_1_out18, decoder_1_out19, decoder_1_out20, decoder_1_out21, decoder_1_out22, decoder_1_out23,
       decoder_1_out24, decoder_1_out25, decoder_1_out26, decoder_1_out27, decoder_1_out28, decoder_1_out29,
       decoder_1_out30, decoder_1_out31;
  wire [31:0] reg64_1_out_5, reg64_1_out_6, reg64_2_out_5, reg64_2_out_6, reg64_3_out_5, reg64_3_out_6,
       reg64_4_out_5, reg64_4_out_6, reg64_5_out_5, reg64_5_out_6, reg64_6_out_5, reg64_6_out_6,
       reg64_7_out_5, reg64_7_out_6, reg64_8_out_5, reg64_8_out_6, reg64_9_out_5, reg64_9_out_6,
       reg64_10_out_5, reg64_10_out_6, reg64_11_out_5, reg64_11_out_6, reg64_12_out_5, reg64_12_out_6,
       reg64_13_out_5, reg64_13_out_6, reg64_14_out_5, reg64_14_out_6, reg64_15_out_5, reg64_15_out_6,
       reg64_16_out_5, reg64_16_out_6, reg64_17_out_5, reg64_17_out_6, reg64_18_out_5, reg64_18_out_6,
       reg64_19_out_5, reg64_19_out_6, reg64_20_out_5, reg64_20_out_6, reg64_21_out_5, reg64_21_out_6,
       reg64_22_out_5, reg64_22_out_6, reg64_23_out_5, reg64_23_out_6, reg64_24_out_5, reg64_24_out_6,
       reg64_25_out_5, reg64_25_out_6, reg64_26_out_5, reg64_26_out_6, reg64_27_out_5, reg64_27_out_6,
       reg64_28_out_5, reg64_28_out_6, reg64_29_out_5, reg64_29_out_6, reg64_30_out_5, reg64_30_out_6,
       reg64_31_out_5, reg64_31_out_6, reg64_32_out_5, reg64_32_out_6;

  Decoder #(.select(5), .disabled(0)) decoder_1 (
    .out0(decoder_1_out0), .out1(decoder_1_out1), .out2(decoder_1_out2), .out3(decoder_1_out3),
    .out4(decoder_1_out4), .out5(decoder_1_out5), .out6(decoder_1_out6), .out7(decoder_1_out7),
    .out8(decoder_1_out8), .out9(decoder_1_out9), .out10(decoder_1_out10), .out11(decoder_1_out11),
    .out12(decoder_1_out12), .out13(decoder_1_out13), .out14(decoder_1_out14), .out15(decoder_1_out15),
    .out16(decoder_1_out16), .out17(decoder_1_out17), .out18(decoder_1_out18), .out19(decoder_1_out19),
    .out20(decoder_1_out20), .out21(decoder_1_out21), .out22(decoder_1_out22), .out23(decoder_1_out23),
    .out24(decoder_1_out24), .out25(decoder_1_out25), .out26(decoder_1_out26), .out27(decoder_1_out27),
    .out28(decoder_1_out28), .out29(decoder_1_out29), .out30(decoder_1_out30), .out31(decoder_1_out31),
    .sel(Write_Register), .en(RegWrite));
  reg64 reg64_1 (.in_3(in_3), .in_4(in_4), .out_5(reg64_1_out_5), .out_6(reg64_1_out_6), .CLK(CLK));  // open: Load
  reg64 reg64_2 (
    .in_3(in_3), .in_4(in_4), .out_5(reg64_2_out_5), .out_6(reg64_2_out_6), .CLK(CLK), .Load(decoder_1_out2));
  reg64 reg64_3 (
    .in_3(in_3), .in_4(in_4), .out_5(reg64_3_out_5), .out_6(reg64_3_out_6), .CLK(CLK), .Load(decoder_1_out4));
  reg64 reg64_4 (
    .in_3(in_3), .in_4(in_4), .out_5(reg64_4_out_5), .out_6(reg64_4_out_6), .CLK(CLK), .Load(decoder_1_out6));
  reg64 reg64_5 (
    .in_3(in_3), .in_4(in_4), .out_5(reg64_5_out_5), .out_6(reg64_5_out_6), .CLK(CLK), .Load(decoder_1_out8));
  reg64 reg64_6 (
    .in_3(in_3), .in_4(in_4), .out_5(reg64_6_out_5), .out_6(reg64_6_out_6), .CLK(CLK), .Load(decoder_1_out10));
  reg64 reg64_7 (
    .in_3(in_3), .in_4(in_4), .out_5(reg64_7_out_5), .out_6(reg64_7_out_6), .CLK(CLK), .Load(decoder_1_out12));
  reg64 reg64_8 (
    .in_3(in_3), .in_4(in_4), .out_5(reg64_8_out_5), .out_6(reg64_8_out_6), .CLK(CLK), .Load(decoder_1_out14));
  reg64 reg64_9 (
    .in_3(in_3), .in_4(in_4), .out_5(reg64_9_out_5), .out_6(reg64_9_out_6), .CLK(CLK), .Load(decoder_1_out16));
  reg64 reg64_10 (
    .in_3(in_3), .in_4(in_4), .out_5(reg64_10_out_5), .out_6(reg64_10_out_6), .CLK(CLK),
    .Load(decoder_1_out18));
  reg64 reg64_11 (
    .in_3(in_3), .in_4(in_4), .out_5(reg64_11_out_5), .out_6(reg64_11_out_6), .CLK(CLK),
    .Load(decoder_1_out20));
  reg64 reg64_12 (
    .in_3(in_3), .in_4(in_4), .out_5(reg64_12_out_5), .out_6(reg64_12_out_6), .CLK(CLK),
    .Load(decoder_1_out22));
  reg64 reg64_13 (
    .in_3(in_3), .in_4(in_4), .out_5(reg64_13_out_5), .out_6(reg64_13_out_6), .CLK(CLK),
    .Load(decoder_1_out24));
  reg64 reg64_14 (
    .in_3(in_3), .in_4(in_4), .out_5(reg64_14_out_5), .out_6(reg64_14_out_6), .CLK(CLK),
    .Load(decoder_1_out26));
  reg64 reg64_15 (
    .in_3(in_3), .in_4(in_4), .out_5(reg64_15_out_5), .out_6(reg64_15_out_6), .CLK(CLK),
    .Load(decoder_1_out28));
  reg64 reg64_16 (
    .in_3(in_3), .in_4(in_4), .out_5(reg64_16_out_5), .out_6(reg64_16_out_6), .CLK(CLK),
    .Load(decoder_1_out30));
  reg64 reg64_17 (
    .in_3(in_3), .in_4(in_4), .out_5(reg64_17_out_5), .out_6(reg64_17_out_6), .CLK(CLK), .Load(decoder_1_out1));
  reg64 reg64_18 (
    .in_3(in_3), .in_4(in_4), .out_5(reg64_18_out_5), .out_6(reg64_18_out_6), .CLK(CLK), .Load(decoder_1_out3));
  reg64 reg64_19 (
    .in_3(in_3), .in_4(in_4), .out_5(reg64_19_out_5), .out_6(reg64_19_out_6), .CLK(CLK), .Load(decoder_1_out5));
  reg64 reg64_20 (
    .in_3(in_3), .in_4(in_4), .out_5(reg64_20_out_5), .out_6(reg64_20_out_6), .CLK(CLK), .Load(decoder_1_out7));
  reg64 reg64_21 (
    .in_3(in_3), .in_4(in_4), .out_5(reg64_21_out_5), .out_6(reg64_21_out_6), .CLK(CLK), .Load(decoder_1_out9));
  reg64 reg64_22 (
    .in_3(in_3), .in_4(in_4), .out_5(reg64_22_out_5), .out_6(reg64_22_out_6), .CLK(CLK),
    .Load(decoder_1_out11));
  reg64 reg64_23 (
    .in_3(in_3), .in_4(in_4), .out_5(reg64_23_out_5), .out_6(reg64_23_out_6), .CLK(CLK),
    .Load(decoder_1_out13));
  reg64 reg64_24 (
    .in_3(in_3), .in_4(in_4), .out_5(reg64_24_out_5), .out_6(reg64_24_out_6), .CLK(CLK),
    .Load(decoder_1_out15));
  reg64 reg64_25 (
    .in_3(in_3), .in_4(in_4), .out_5(reg64_25_out_5), .out_6(reg64_25_out_6), .CLK(CLK),
    .Load(decoder_1_out17));
  reg64 reg64_26 (
    .in_3(in_3), .in_4(in_4), .out_5(reg64_26_out_5), .out_6(reg64_26_out_6), .CLK(CLK),
    .Load(decoder_1_out19));
  reg64 reg64_27 (
    .in_3(in_3), .in_4(in_4), .out_5(reg64_27_out_5), .out_6(reg64_27_out_6), .CLK(CLK),
    .Load(decoder_1_out21));
  reg64 reg64_28 (
    .in_3(in_3), .in_4(in_4), .out_5(reg64_28_out_5), .out_6(reg64_28_out_6), .CLK(CLK),
    .Load(decoder_1_out23));
  reg64 reg64_29 (
    .in_3(in_3), .in_4(in_4), .out_5(reg64_29_out_5), .out_6(reg64_29_out_6), .CLK(CLK),
    .Load(decoder_1_out25));
  reg64 reg64_30 (
    .in_3(in_3), .in_4(in_4), .out_5(reg64_30_out_5), .out_6(reg64_30_out_6), .CLK(CLK),
    .Load(decoder_1_out27));
  reg64 reg64_31 (
    .in_3(in_3), .in_4(in_4), .out_5(reg64_31_out_5), .out_6(reg64_31_out_6), .CLK(CLK),
    .Load(decoder_1_out29));
  reg64 reg64_32 (
    .in_3(in_3), .in_4(in_4), .out_5(reg64_32_out_5), .out_6(reg64_32_out_6), .CLK(CLK),
    .Load(decoder_1_out31));
  Multiplexer #(.select(5), .width(32)) multiplexer_1 (
    .in0(reg64_1_out_6), .in1(reg64_17_out_6), .in2(reg64_2_out_6), .in3(reg64_18_out_6),
    .in4(reg64_3_out_6), .in5(reg64_19_out_6), .in6(reg64_4_out_6), .in7(reg64_20_out_6),
    .in8(reg64_5_out_6), .in9(reg64_21_out_6), .in10(reg64_6_out_6), .in11(reg64_22_out_6),
    .in12(reg64_7_out_6), .in13(reg64_23_out_6), .in14(reg64_8_out_6), .in15(reg64_24_out_6),
    .in16(reg64_9_out_6), .in17(reg64_25_out_6), .in18(reg64_10_out_6), .in19(reg64_26_out_6),
    .in20(reg64_11_out_6), .in21(reg64_27_out_6), .in22(reg64_12_out_6), .in23(reg64_28_out_6),
    .in24(reg64_13_out_6), .in25(reg64_29_out_6), .in26(reg64_14_out_6), .in27(reg64_30_out_6),
    .in28(reg64_15_out_6), .in29(reg64_31_out_6), .in30(reg64_16_out_6), .in31(reg64_32_out_6), .out(out_9),
    .sel(read_register1));  // open: en
  Multiplexer #(.select(5), .width(32)) multiplexer_2 (
    .in0(reg64_1_out_6), .in1(reg64_17_out_6), .in2(reg64_2_out_6), .in3(reg64_18_out_6),
    .in4(reg64_3_out_6), .in5(reg64_19_out_6), .in6(reg64_4_out_6), .in7(reg64_20_out_6),
    .in8(reg64_5_out_6), .in9(reg64_21_out_6), .in10(reg64_6_out_6), .in11(reg64_22_out_6),
    .in12(reg64_7_out_6), .in13(reg64_23_out_6), .in14(reg64_8_out_6), .in15(reg64_24_out_6),
    .in16(reg64_9_out_6), .in17(reg64_25_out_6), .in18(reg64_10_out_6), .in19(reg64_26_out_6),
    .in20(reg64_11_out_6), .in21(reg64_27_out_6), .in22(reg64_12_out_6), .in23(reg64_28_out_6),
    .in24(reg64_13_out_6), .in25(reg64_29_out_6), .in26(reg64_14_out_6), .in27(reg64_30_out_6),
    .in28(reg64_15_out_6), .in29(reg64_31_out_6), .in30(reg64_16_out_6), .in31(reg64_32_out_6), .out(out_11),
    .sel(read_register2));  // open: en
  Multiplexer #(.select(5), .width(32)) multiplexer_3 (
    .in0(reg64_1_out_5), .in1(reg64_17_out_5), .in2(reg64_2_out_5), .in3(reg64_18_out_5),
    .in4(reg64_3_out_5), .in5(reg64_19_out_5), .in6(reg64_4_out_5), .in7(reg64_20_out_5),
    .in8(reg64_5_out_5), .in9(reg64_21_out_5), .in10(reg64_6_out_5), .in11(reg64_22_out_5),
    .in12(reg64_7_out_5), .in13(reg64_23_out_5), .in14(reg64_8_out_5), .in15(reg64_24_out_5),
    .in16(reg64_9_out_5), .in17(reg64_25_out_5), .in18(reg64_10_out_5), .in19(reg64_26_out_5),
    .in20(reg64_11_out_5), .in21(reg64_27_out_5), .in22(reg64_12_out_5), .in23(reg64_28_out_5),
    .in24(reg64_13_out_5), .in25(reg64_29_out_5), .in26(reg64_14_out_5), .in27(reg64_30_out_5),
    .in28(reg64_15_out_5), .in29(reg64_31_out_5), .in30(reg64_16_out_5), .in31(reg64_32_out_5), .out(out_8),
    .sel(read_register1));  // open: en
  Multiplexer #(.select(5), .width(32)) multiplexer_4 (
    .in0(reg64_1_out_5), .in1(reg64_17_out_5), .in2(reg64_2_out_5), .in3(reg64_18_out_5),
    .in4(reg64_3_out_5), .in5(reg64_19_out_5), .in6(reg64_4_out_5), .in7(reg64_20_out_5),
    .in8(reg64_5_out_5), .in9(reg64_21_out_5), .in10(reg64_6_out_5), .in11(reg64_22_out_5),
    .in12(reg64_7_out_5), .in13(reg64_23_out_5), .in14(reg64_8_out_5), .in15(reg64_24_out_5),
    .in16(reg64_9_out_5), .in17(reg64_25_out_5), .in18(reg64_10_out_5), .in19(reg64_26_out_5),
    .in20(reg64_11_out_5), .in21(reg64_27_out_5), .in22(reg64_12_out_5), .in23(reg64_28_out_5),
    .in24(reg64_13_out_5), .in25(reg64_29_out_5), .in26(reg64_14_out_5), .in27(reg64_30_out_5),
    .in28(reg64_15_out_5), .in29(reg64_31_out_5), .in30(reg64_16_out_5), .in31(reg64_32_out_5), .out(out_10),
    .sel(read_register2));  // open: en

  // Notes on the sheet:
  //   write data
  //   read data 1
  //   read data2
endmodule

module reg64 (
  input  CLK,
  input  Load,
  input  [31:0] in_3,
  input  [31:0] in_4,
  output [31:0] out_5,
  output [31:0] out_6
);

  wire and_1_out;

  and and_1 (and_1_out, CLK, Load);
  D_Flip_Flop d_ff_1 (.clk(and_1_out), .D(in_3[0]), .Q(out_5[0]));  // open: Qn, preset, en, reset
  D_Flip_Flop d_ff_2 (.clk(and_1_out), .D(in_3[8]), .Q(out_5[8]));  // open: Qn, preset, en, reset
  D_Flip_Flop d_ff_3 (.clk(and_1_out), .D(in_3[16]), .Q(out_5[16]));  // open: Qn, preset, en, reset
  D_Flip_Flop d_ff_4 (.clk(and_1_out), .D(in_3[24]), .Q(out_5[24]));  // open: Qn, preset, en, reset
  D_Flip_Flop d_ff_5 (.clk(and_1_out), .D(in_4[0]), .Q(out_6[0]));  // open: Qn, preset, en, reset
  D_Flip_Flop d_ff_6 (.clk(and_1_out), .D(in_4[8]), .Q(out_6[8]));  // open: Qn, preset, en, reset
  D_Flip_Flop d_ff_7 (.clk(and_1_out), .D(in_4[16]), .Q(out_6[16]));  // open: Qn, preset, en, reset
  D_Flip_Flop d_ff_8 (.clk(and_1_out), .D(in_4[24]), .Q(out_6[24]));  // open: Qn, preset, en, reset
  D_Flip_Flop d_ff_9 (.clk(and_1_out), .D(in_3[1]), .Q(out_5[1]));  // open: Qn, preset, en, reset
  D_Flip_Flop d_ff_10 (.clk(and_1_out), .D(in_3[9]), .Q(out_5[9]));  // open: Qn, preset, en, reset
  D_Flip_Flop d_ff_11 (.clk(and_1_out), .D(in_3[17]), .Q(out_5[17]));  // open: Qn, preset, en, reset
  D_Flip_Flop d_ff_12 (.clk(and_1_out), .D(in_3[25]), .Q(out_5[25]));  // open: Qn, preset, en, reset
  D_Flip_Flop d_ff_13 (.clk(and_1_out), .D(in_4[1]), .Q(out_6[1]));  // open: Qn, preset, en, reset
  D_Flip_Flop d_ff_14 (.clk(and_1_out), .D(in_4[9]), .Q(out_6[9]));  // open: Qn, preset, en, reset
  D_Flip_Flop d_ff_15 (.clk(and_1_out), .D(in_4[17]), .Q(out_6[17]));  // open: Qn, preset, en, reset
  D_Flip_Flop d_ff_16 (.clk(and_1_out), .D(in_4[25]), .Q(out_6[25]));  // open: Qn, preset, en, reset
  D_Flip_Flop d_ff_17 (.clk(and_1_out), .D(in_3[2]), .Q(out_5[2]));  // open: Qn, preset, en, reset
  D_Flip_Flop d_ff_18 (.clk(and_1_out), .D(in_3[10]), .Q(out_5[10]));  // open: Qn, preset, en, reset
  D_Flip_Flop d_ff_19 (.clk(and_1_out), .D(in_3[18]), .Q(out_5[18]));  // open: Qn, preset, en, reset
  D_Flip_Flop d_ff_20 (.clk(and_1_out), .D(in_3[26]), .Q(out_5[26]));  // open: Qn, preset, en, reset
  D_Flip_Flop d_ff_21 (.clk(and_1_out), .D(in_4[2]), .Q(out_6[2]));  // open: Qn, preset, en, reset
  D_Flip_Flop d_ff_22 (.clk(and_1_out), .D(in_4[10]), .Q(out_6[10]));  // open: Qn, preset, en, reset
  D_Flip_Flop d_ff_23 (.clk(and_1_out), .D(in_4[18]), .Q(out_6[18]));  // open: Qn, preset, en, reset
  D_Flip_Flop d_ff_24 (.clk(and_1_out), .D(in_4[26]), .Q(out_6[26]));  // open: Qn, preset, en, reset
  D_Flip_Flop d_ff_25 (.clk(and_1_out), .D(in_3[3]), .Q(out_5[3]));  // open: Qn, preset, en, reset
  D_Flip_Flop d_ff_26 (.clk(and_1_out), .D(in_3[11]), .Q(out_5[11]));  // open: Qn, preset, en, reset
  D_Flip_Flop d_ff_27 (.clk(and_1_out), .D(in_3[19]), .Q(out_5[19]));  // open: Qn, preset, en, reset
  D_Flip_Flop d_ff_28 (.clk(and_1_out), .D(in_3[27]), .Q(out_5[27]));  // open: Qn, preset, en, reset
  D_Flip_Flop d_ff_29 (.clk(and_1_out), .D(in_4[3]), .Q(out_6[3]));  // open: Qn, preset, en, reset
  D_Flip_Flop d_ff_30 (.clk(and_1_out), .D(in_4[11]), .Q(out_6[11]));  // open: Qn, preset, en, reset
  D_Flip_Flop d_ff_31 (.clk(and_1_out), .D(in_4[19]), .Q(out_6[19]));  // open: Qn, preset, en, reset
  D_Flip_Flop d_ff_32 (.clk(and_1_out), .D(in_4[27]), .Q(out_6[27]));  // open: Qn, preset, en, reset
  D_Flip_Flop d_ff_33 (.clk(and_1_out), .D(in_3[4]), .Q(out_5[4]));  // open: Qn, preset, en, reset
  D_Flip_Flop d_ff_34 (.clk(and_1_out), .D(in_3[12]), .Q(out_5[12]));  // open: Qn, preset, en, reset
  D_Flip_Flop d_ff_35 (.clk(and_1_out), .D(in_3[20]), .Q(out_5[20]));  // open: Qn, preset, en, reset
  D_Flip_Flop d_ff_36 (.clk(and_1_out), .D(in_3[28]), .Q(out_5[28]));  // open: Qn, preset, en, reset
  D_Flip_Flop d_ff_37 (.clk(and_1_out), .D(in_4[4]), .Q(out_6[4]));  // open: Qn, preset, en, reset
  D_Flip_Flop d_ff_38 (.clk(and_1_out), .D(in_4[12]), .Q(out_6[12]));  // open: Qn, preset, en, reset
  D_Flip_Flop d_ff_39 (.clk(and_1_out), .D(in_4[20]), .Q(out_6[20]));  // open: Qn, preset, en, reset
  D_Flip_Flop d_ff_40 (.clk(and_1_out), .D(in_4[28]), .Q(out_6[28]));  // open: Qn, preset, en, reset
  D_Flip_Flop d_ff_41 (.clk(and_1_out), .D(in_3[5]), .Q(out_5[5]));  // open: Qn, preset, en, reset
  D_Flip_Flop d_ff_42 (.clk(and_1_out), .D(in_3[13]), .Q(out_5[13]));  // open: Qn, preset, en, reset
  D_Flip_Flop d_ff_43 (.clk(and_1_out), .D(in_3[21]), .Q(out_5[21]));  // open: Qn, preset, en, reset
  D_Flip_Flop d_ff_44 (.clk(and_1_out), .D(in_3[29]), .Q(out_5[29]));  // open: Qn, preset, en, reset
  D_Flip_Flop d_ff_45 (.clk(and_1_out), .D(in_4[5]), .Q(out_6[5]));  // open: Qn, preset, en, reset
  D_Flip_Flop d_ff_46 (.clk(and_1_out), .D(in_4[13]), .Q(out_6[13]));  // open: Qn, preset, en, reset
  D_Flip_Flop d_ff_47 (.clk(and_1_out), .D(in_4[21]), .Q(out_6[21]));  // open: Qn, preset, en, reset
  D_Flip_Flop d_ff_48 (.clk(and_1_out), .D(in_4[29]), .Q(out_6[29]));  // open: Qn, preset, en, reset
  D_Flip_Flop d_ff_49 (.clk(and_1_out), .D(in_3[6]), .Q(out_5[6]));  // open: Qn, preset, en, reset
  D_Flip_Flop d_ff_50 (.clk(and_1_out), .D(in_3[14]), .Q(out_5[14]));  // open: Qn, preset, en, reset
  D_Flip_Flop d_ff_51 (.clk(and_1_out), .D(in_3[22]), .Q(out_5[22]));  // open: Qn, preset, en, reset
  D_Flip_Flop d_ff_52 (.clk(and_1_out), .D(in_3[30]), .Q(out_5[30]));  // open: Qn, preset, en, reset
  D_Flip_Flop d_ff_53 (.clk(and_1_out), .D(in_4[6]), .Q(out_6[6]));  // open: Qn, preset, en, reset
  D_Flip_Flop d_ff_54 (.clk(and_1_out), .D(in_4[14]), .Q(out_6[14]));  // open: Qn, preset, en, reset
  D_Flip_Flop d_ff_55 (.clk(and_1_out), .D(in_4[22]), .Q(out_6[22]));  // open: Qn, preset, en, reset
  D_Flip_Flop d_ff_56 (.clk(and_1_out), .D(in_4[30]), .Q(out_6[30]));  // open: Qn, preset, en, reset
  D_Flip_Flop d_ff_57 (.clk(and_1_out), .D(in_3[7]), .Q(out_5[7]));  // open: Qn, preset, en, reset
  D_Flip_Flop d_ff_58 (.clk(and_1_out), .D(in_3[15]), .Q(out_5[15]));  // open: Qn, preset, en, reset
  D_Flip_Flop d_ff_59 (.clk(and_1_out), .D(in_3[23]), .Q(out_5[23]));  // open: Qn, preset, en, reset
  D_Flip_Flop d_ff_60 (.clk(and_1_out), .D(in_3[31]), .Q(out_5[31]));  // open: Qn, preset, en, reset
  D_Flip_Flop d_ff_61 (.clk(and_1_out), .D(in_4[7]), .Q(out_6[7]));  // open: Qn, preset, en, reset
  D_Flip_Flop d_ff_62 (.clk(and_1_out), .D(in_4[15]), .Q(out_6[15]));  // open: Qn, preset, en, reset
  D_Flip_Flop d_ff_63 (.clk(and_1_out), .D(in_4[23]), .Q(out_6[23]));  // open: Qn, preset, en, reset
  D_Flip_Flop d_ff_64 (.clk(and_1_out), .D(in_4[31]), .Q(out_6[31]));  // open: Qn, preset, en, reset
endmodule
